# Fritzing sketch 1a (saved by Fritzing 0.9.3b)
breadboards: 1

parts:
  IC1 = IC, DIP package, 14 pins [chip_label=74HC00]
  IC2 = IC, DIP package, 14 pins [chip_label=74HC20]

nets:
  N1: IC1.pin1, IC2.pin5
  N2: IC1.pin2, IC2.pin2
  N3: IC1.pin3, IC1.pin13
  N4: IC1.pin4, IC1.pin12
  N5: IC1.pin5, IC2.pin4
  N6: IC1.pin6, IC2.pin1
  N7: IC1.pin7, IC2.pin7
  N8: IC1.pin9, IC2.pin6
  N9: IC1.pin10, IC1.pin11
  N10: IC1.pin14, IC2.pin14
